// Logisim project main.circ as structural Verilog: 2 circuits, main circuit main
module main (
);

  wire A_out, addr7, and_1_out, and_2_out, and_3_out, cdm_8_mark5_1_p3, cdm_8_mark5_1_p4, D_out, mem,
       or_1_out, R_out, r_w, S_out, tact, W_out;
  wire [1:0] multiplexer_1_out, or_2_out;
  wire [3:0] apple_X, apple_Y;
  wire [6:0] adr;
  wire [7:0] data_in, data_out, data_out_p;
  wire [15:0] gpu_nvidia_geforce_rtx_4090ti_1_row_1, gpu_nvidia_geforce_rtx_4090ti_1_row_2,
       gpu_nvidia_geforce_rtx_4090ti_1_row_3, gpu_nvidia_geforce_rtx_4090ti_1_row_4,
       gpu_nvidia_geforce_rtx_4090ti_1_row_5, gpu_nvidia_geforce_rtx_4090ti_1_row_6,
       gpu_nvidia_geforce_rtx_4090ti_1_row_7, gpu_nvidia_geforce_rtx_4090ti_1_row_8,
       gpu_nvidia_geforce_rtx_4090ti_1_row_9, gpu_nvidia_geforce_rtx_4090ti_1_row_10,
       gpu_nvidia_geforce_rtx_4090ti_1_row_11, gpu_nvidia_geforce_rtx_4090ti_1_row_12,
       gpu_nvidia_geforce_rtx_4090ti_1_row_13, gpu_nvidia_geforce_rtx_4090ti_1_row_14,
       gpu_nvidia_geforce_rtx_4090ti_1_row_15, gpu_nvidia_geforce_rtx_4090ti_1_row_16;

  Clock clock_1 (.out(tact));
  Multiplexer #(.width(2), .enable("false")) multiplexer_1 (
    .in0(2'b00), .in1(or_2_out), .out(multiplexer_1_out), .sel(or_1_out));
  DotMatrix #(.inputtype("row"), .matrixcols(16), .matrixrows(16)) dotmatrix_1 (
    .row0(gpu_nvidia_geforce_rtx_4090ti_1_row_1), .row1(gpu_nvidia_geforce_rtx_4090ti_1_row_2),
    .row2(gpu_nvidia_geforce_rtx_4090ti_1_row_3), .row3(gpu_nvidia_geforce_rtx_4090ti_1_row_4),
    .row4(gpu_nvidia_geforce_rtx_4090ti_1_row_5), .row5(gpu_nvidia_geforce_rtx_4090ti_1_row_6),
    .row6(gpu_nvidia_geforce_rtx_4090ti_1_row_7), .row7(gpu_nvidia_geforce_rtx_4090ti_1_row_8),
    .row8(gpu_nvidia_geforce_rtx_4090ti_1_row_9), .row9(gpu_nvidia_geforce_rtx_4090ti_1_row_10),
    .row10(gpu_nvidia_geforce_rtx_4090ti_1_row_11), .row11(gpu_nvidia_geforce_rtx_4090ti_1_row_12),
    .row12(gpu_nvidia_geforce_rtx_4090ti_1_row_13), .row13(gpu_nvidia_geforce_rtx_4090ti_1_row_14),
    .row14(gpu_nvidia_geforce_rtx_4090ti_1_row_15), .row15(gpu_nvidia_geforce_rtx_4090ti_1_row_16));
  GPU_Nvidia_Geforce_RTX_4090TI gpu_nvidia_geforce_rtx_4090ti_1 (
    .row_1(gpu_nvidia_geforce_rtx_4090ti_1_row_1), .row_2(gpu_nvidia_geforce_rtx_4090ti_1_row_2),
    .row_3(gpu_nvidia_geforce_rtx_4090ti_1_row_3), .row_4(gpu_nvidia_geforce_rtx_4090ti_1_row_4),
    .row_5(gpu_nvidia_geforce_rtx_4090ti_1_row_5), .row_6(gpu_nvidia_geforce_rtx_4090ti_1_row_6),
    .row_7(gpu_nvidia_geforce_rtx_4090ti_1_row_7), .row_8(gpu_nvidia_geforce_rtx_4090ti_1_row_8),
    .row_9(gpu_nvidia_geforce_rtx_4090ti_1_row_9), .row_10(gpu_nvidia_geforce_rtx_4090ti_1_row_10),
    .row_11(gpu_nvidia_geforce_rtx_4090ti_1_row_11), .row_12(gpu_nvidia_geforce_rtx_4090ti_1_row_12),
    .row_13(gpu_nvidia_geforce_rtx_4090ti_1_row_13), .row_14(gpu_nvidia_geforce_rtx_4090ti_1_row_14),
    .row_15(gpu_nvidia_geforce_rtx_4090ti_1_row_15), .row_16(gpu_nvidia_geforce_rtx_4090ti_1_row_16),
    .apple_X(apple_X), .apple_Y(apple_Y));
  or or_1 (or_1_out, W_out, A_out, S_out, S_out);
  or or_2 (or_2_out[0], A_out, S_out);
  or or_3 (or_2_out[1], S_out, D_out);
  Button W (.out(W_out));
  Button A (.out(A_out));
  Button S (.out(S_out));
  and and_1 (and_1_out, addr7, r_w);
  Button R (.out(R_out));
  Button D (.out(D_out));
  generator_apple generator_apple_1 (.in_1(R_out), .apple_Y(apple_X));  // open: apple_X
  generator_apple generator_apple_2 (.in_1(R_out), .apple_X(apple_Y));  // open: apple_Y
  and and_2 (and_2_out, ~addr7, mem);  // AND_Gate
  // CdM_8_mark5 cdm_8_mark5_1: pin names not known; wires that end beside it: 3'b000, tact, cdm_8_mark5_1_p3, cdm_8_mark5_1_p4, {addr7, adr}, data_out, data_in
  RAM #(.bus("separate")) ram_1 (
    .addr({addr7, adr}), .data(data_out), .str(and_1_out), .sel(1'b1), .clk(tact), .ld(and_3_out), .clr(1'b0));  // open: din
  and and_3 (and_3_out, mem, addr7);
  ROM rom_1 (.addr({addr7, adr}), .data(data_out_p), .sel(and_2_out));
  and and_4 (mem, cdm_8_mark5_1_p3, cdm_8_mark5_1_p4);
  and and_5 (r_w, cdm_8_mark5_1_p3, ~cdm_8_mark5_1_p4);  // AND_Gate
  Multiplexer #(.width(8), .enable("false")) multiplexer_2 (
    .in0(data_out_p), .in1(data_out), .out(data_in), .sel(addr7));

  // Other names for the same wires on the sheet: adr[7] = addr7

  // Notes on the sheet:
  //   contents of rom_1 (hex, n*v repeats v):
  //   d0 62 b0 0 e1 13 d1 60 b5 8d d3 f 77 ed 10 35 d2 60 a9 d1 1 71 e1 25 d1 5f b5 8d d3 f 77 ed 22 35 d2
  //   5f a9 d1 2 71 e1 36 d1 5f b5 89 5 ea 33 d1 f d2 5f a9 d1 3 71 e1 47 d1 60 b5 89 5 ea 44 d1 f d2 60
  //   a9 d0 5f b0 d1 63 b5 a4 d0 60 b0 d1 64 b5 a4 d0 63 b0 b0 d0 64 b0 b0 ee 0 0 0 1 0 f0 f1
endmodule

module generator_apple (
  input  in_1,
  output [3:0] apple_X,
  output [3:0] apple_Y
);

  wire _00_checker, and_1_out, comparator_1_eq, comparator_2_eq;
  wire [3:0] random_1_out, random_2_out, transistor_1_out, transistor_2_out;

  Random #(.width(4)) random_1 (.clk(in_1), .out(random_1_out));  // open: next, clr
  Random #(.width(4)) random_2 (.clk(in_1), .out(random_2_out));  // open: next, clr
  Transistor #(.width(4)) transistor_1 (.in(random_2_out), .out(transistor_1_out), .gate(_00_checker));
  Transistor #(.width(4)) transistor_2 (.in(random_1_out), .out(transistor_2_out), .gate(_00_checker));
  Comparator #(.width(4)) comparator_1 (.a(random_1_out), .b(random_2_out), .eq(comparator_1_eq));  // open: gt, lt
  Comparator #(.width(4)) comparator_2 (.a(random_2_out), .b(4'b0000), .eq(comparator_2_eq));  // open: gt, lt
  not not_1 (_00_checker, and_1_out);
  and and_1 (and_1_out, comparator_1_eq, comparator_2_eq);
  Transistor #(.width(4)) transistor_3 (.in(random_1_out), .out(apple_X), .gate(and_1_out));
  Adder #(.width(4)) adder_1 (.a(transistor_1_out), .b(4'b0001), .out(apple_Y));  // open: cin, cout
  Adder #(.width(4)) adder_2 (.a(transistor_2_out), .b(4'b0001), .out(apple_X));  // open: cin, cout
  Transistor #(.width(4)) transistor_4 (.in(random_2_out), .out(apple_Y), .gate(and_1_out));
endmodule
